# Fritzing sketch led (saved by Fritzing 0.9.3b)
breadboards: 1

parts:
  パーツ1 = Arduino Uno (Rev3) - ICSP
  R1 = Resistor [tolerance=±5% resistance=220 package=THT]
  LED1 = smd LED [color="Red (633nm)" package="0805 [SMD]"]

nets:
  N1: パーツ1.GND, パーツ1.D13/SCK, R1.Pin_0, LED1.anode
  N2: R1.Pin_1, LED1.cathode
